// Digital circuit PC_ROM_SPLITTER_4_REGS.dig as structural Verilog
module PC_ROM_SPLITTER_4_REGS (
  input  clk,
  input  PC_RESET,
  input  C_I,
  output [3:0] op_code,
  output [3:0] RS,
  output [19:0] addr,
  output addr_carry,
  output [3:0] RD,
  output [19:0] DATA,
  output [31:0] CUR_INST_DATA
);

  wire op_add, op_write;
  wire [7:0] PC_out;
  wire [19:0] driver_1_out, driver_2_out, registerfile_1_da, registerfile_1_db;

  Counter #(.Bits(8)) PC (.en(clk), .C(clk), .clr(PC_RESET), .out(PC_out));  // open: ovf
  ROM #(.AddrBits(8), .Bits(32)) INSTR_MEM (.A(PC_out), .sel(1'b1), .D(CUR_INST_DATA));
  RegisterFile #(.AddrBits(4), .Bits(20)) registerfile_1 (
    .Din(CUR_INST_DATA[19:0]), .we(op_write), .Rw(CUR_INST_DATA[27:24]), .C(clk), .Ra(CUR_INST_DATA[27:24]),
    .Rb(CUR_INST_DATA[23:20]), .Da(registerfile_1_da), .Db(registerfile_1_db));
  Decoder #(.Selector_Bits(4)) decoder_1 (
    .sel(CUR_INST_DATA[31:28]), .out_0(op_write), .out_1(op_add));  // open: out_2, out_3, out_4, out_5, out_6, out_7, out_8, out_9, out_10, out_11, out_12, out_13, out_14, out_15
  assign driver_1_out = op_add ? registerfile_1_da : 20'bz;  // Driver driver_1
  assign driver_2_out = op_add ? registerfile_1_db : 20'bz;  // Driver driver_2
  Add #(.Bits(20)) add_1 (.a(driver_1_out), .b(driver_2_out), .c_i(C_I), .s(addr), .c_o(addr_carry));

  assign DATA = CUR_INST_DATA[19:0];
  assign op_code = CUR_INST_DATA[31:28];
  assign RD = CUR_INST_DATA[27:24];
  assign RS = CUR_INST_DATA[23:20];

  // Other names for the same wires on the sheet: C = clk; CARRY = addr_carry; inst_bin[31:0] = CUR_INST_DATA;
  //   OP[3:0] = CUR_INST_DATA[31:28]; reset = PC_RESET

  // Notes on the sheet:
  //   contents of INSTR_MEM (hex, n*v repeats v):
  //   100000a,2000014,13100000
endmodule
